// Digital circuit CPU.dig as structural Verilog
module CPU (
  input  [10:0] in_1,
  input  in_2,
  input  [7:0] in_3,
  input  [2:0] OpCode
);

  wire alu_1_of, alu_1_of2, button_1_out, contador3bits_1_clk, not_1_out, not_2_out;
  wire [2:0] contador3bits_1_q0;
  wire [3:0] registrador8bits_1_q, registrador8bits_1_q_2, registrador8bits_2_q;
  wire [7:0] alu_1_ac_out, alu_1_mq;
  wire [7:4] registrador8bits_2_q_2;
  wire [10:0] eepromdualport_1_d;

  contador3bits contador3bits_1 (
    .C(button_1_out), .Q0(contador3bits_1_q0[0]), .Q1(contador3bits_1_q0[1]), .Q2(contador3bits_1_q0[2]),
    .CLK(contador3bits_1_clk));
  Button button_1 (.out(button_1_out));
  EEPROMDualPort #(.AddrBits(6), .Bits(11)) eepromdualport_1 (
    .A({OpCode, contador3bits_1_q0}), .Din(in_1), .str(1'b0), .C(button_1_out), .ld(1'b1),
    .D(eepromdualport_1_d));
  not not_1 (not_1_out, contador3bits_1_clk);
  ALU alu_1 (
    .N(eepromdualport_1_d[7:0]), .AC({registrador8bits_1_q_2, registrador8bits_1_q}), .Shift(in_2),
    .MQSel(in_3), .B3(eepromdualport_1_d[10]), .B2(eepromdualport_1_d[9]), .B1(eepromdualport_1_d[8]),
    .Of(alu_1_of), .Of2(alu_1_of2), .AC_out(alu_1_ac_out), .MQ(alu_1_mq));
  not not_2 (not_2_out, contador3bits_1_clk);
  LED led_1 (.in(alu_1_of));
  LED led_2 (.in(alu_1_of2));
  registrador8bits registrador8bits_1 (
    .D(alu_1_ac_out), .CLK(not_1_out), .En(1'b1), .Q({registrador8bits_1_q_2, registrador8bits_1_q}));
  registrador8bits registrador8bits_2 (
    .D(alu_1_mq), .CLK(not_2_out), .En(1'b1), .Q({registrador8bits_2_q_2, registrador8bits_2_q}));
  Seven_Seg_Hex seven_seg_hex_1 (.d(registrador8bits_1_q_2), .dp(1'b0));
  Seven_Seg_Hex seven_seg_hex_2 (.d(registrador8bits_2_q_2), .dp(1'b0));
  Seven_Seg_Hex seven_seg_hex_3 (.d(registrador8bits_1_q), .dp(1'b0));
  Seven_Seg_Hex seven_seg_hex_4 (.d(registrador8bits_2_q), .dp(1'b0));

  // Notes on the sheet:
  //   contents of eepromdualport_1 (hex, n*v repeats v):
  //   f,a,105,603,407,500
  //   000 - Soma
  //   001 - Subtração
  //   010 - Multiplicação
  //   011 - Divisão
  //   100 - Shift
  //   Reg AC
  //   Reg MQ
endmodule
